// Logisim project tv-tennis.circ as structural Verilog: 13 circuits, main circuit main
module main (
  output Collision,
  output isVyActive,
  output Vy,
  output Vx,
  output [4:0] ballY
);

  wire and_1_out, and_2_out, and_3_out, and_4_out, and_5_out, and_6_out, and_7_out, and_8_out, and_9_out,
       and_10_out, cdm_8_mark5_1_p1, cdm_8_mark5_1_p3, cdm_8_mark5_1_p4, cdm_8_mark5_1_p6, cdm_8_mark5_1_p7,
       cdm_8_mark5_1_p8, cdm_8_mark5_1_p9, cdm_8_mark5_1_p10, cdm_8_mark5_1_p11, Cl, clock_2_out,
       clock_3_out, clock_4_out, code, comparator_1_eq, comparator_2_eq, comparator_3_eq, comparator_4_eq,
       comparator_5_eq, data, kinematic_controller_1_gol, kinematic_controller_1_vy, mem, not_1_out,
       not_2_out, or_1_out, or_2_out, R_out, rd_wr_prime, register_3_q;
  wire [3:0] n10_1__1, n10_1__10, n10_2__1, n10_2__10;
  wire [4:0] bit_extender_5_out, joystick_1_y, kinematic_controller_1_ballx, kinematic_controller_1_bally,
       kinematic_controller_1_chipid, kinematic_controller_1_leftbaty, kinematic_controller_1_rightbaty,
       randbatpos_1_randbatpos, register_2_q;
  wire [6:0] L, R;
  wire [7:0] bit_extender_1_out, bit_extender_2_out, bit_extender_3_out, bit_extender_4_out,
       cdm_8_mark5_1_p14, cdm_8_mark5_1_p15, cdm_8_mark5_1_p16, controlled_buffer_1_out, register_1_q;
  wire [31:0] chipset_1_bus_0, chipset_1_bus_0_2, chipset_1_bus_0_3, chipset_1_bus_0_4, chipset_1_bus_0_5,
       chipset_1_bus_0_6, chipset_1_bus_0_7, chipset_1_bus_0_8, chipset_1_bus_0_9, chipset_1_bus_0_10,
       chipset_1_bus_0_11, chipset_1_bus_0_12, chipset_1_bus_0_13, chipset_1_bus_0_14, chipset_1_bus_0_15,
       chipset_1_bus_0_16, chipset_1_bus_0_17, chipset_1_bus_0_18, chipset_1_bus_0_19, chipset_1_bus_0_20,
       chipset_1_bus_0_21, chipset_1_bus_0_22, chipset_1_bus_0_23, chipset_1_bus_0_24, chipset_1_bus_0_25,
       chipset_1_bus_0_26, chipset_1_bus_0_27, chipset_1_bus_0_28, chipset_1_bus_0_29, chipset_1_bus_0_30,
       chipset_1_bus_0_31, chipset_1_bus_0_32;

  // Probe on cdm_8_mark5_1_p3
  // Probe on cdm_8_mark5_1_p4
  // Probe on cdm_8_mark5_1_p6
  // Probe on cdm_8_mark5_1_p7
  and and_1 (and_1_out, Cl, Collision);
  Clock clock_1 (.out(Cl));
  // Probe on cdm_8_mark5_1_p9
  // Probe on cdm_8_mark5_1_p8
  // Probe on cdm_8_mark5_1_p10
  // CdM_8_mark5 cdm_8_mark5_1: pin names not known; wires that end beside it: cdm_8_mark5_1_p1, cdm_8_mark5_1_p1, cdm_8_mark5_1_p3, cdm_8_mark5_1_p4, and_1_out, cdm_8_mark5_1_p6, cdm_8_mark5_1_p7, cdm_8_mark5_1_p8, cdm_8_mark5_1_p9, cdm_8_mark5_1_p10, cdm_8_mark5_1_p11, mem, rd_wr_prime, cdm_8_mark5_1_p14, cdm_8_mark5_1_p15, cdm_8_mark5_1_p16
  and and_2 (and_2_out, data, rd_wr_prime, comparator_1_eq);
  Comparator comparator_1 (.a(cdm_8_mark5_1_p14), .b(8'h1), .eq(comparator_1_eq));  // open: gt, lt
  and and_3 (and_3_out, data, rd_wr_prime, comparator_2_eq);
  Comparator comparator_2 (.a(cdm_8_mark5_1_p14), .b(8'h2), .eq(comparator_2_eq));  // open: gt, lt
  and and_4 (and_4_out, data, rd_wr_prime, comparator_3_eq);
  Comparator comparator_3 (.a(cdm_8_mark5_1_p14), .b(8'h3), .eq(comparator_3_eq));  // open: gt, lt
  and and_5 (and_5_out, data, rd_wr_prime, comparator_4_eq);
  Comparator comparator_4 (.a(cdm_8_mark5_1_p14), .b(8'h4), .eq(comparator_4_eq));  // open: gt, lt
  Decoder decoder_1 (.out0(code), .out1(data), .sel(cdm_8_mark5_1_p11), .en(mem));
  assign controlled_buffer_1_out = not_1_out ? cdm_8_mark5_1_p15 : 8'bz;  // Controlled_Buffer controlled_buffer_1
  not not_1 (not_1_out, rd_wr_prime);
  assign cdm_8_mark5_1_p16 = rd_wr_prime ? controlled_buffer_1_out : 8'bz;  // Controlled_Buffer controlled_buffer_2
  assign controlled_buffer_1_out = and_5_out ? bit_extender_4_out : 8'bz;  // Controlled_Buffer controlled_buffer_3
  and and_6 (and_6_out, data, ~or_1_out);  // AND_Gate
  assign controlled_buffer_1_out = and_2_out ? bit_extender_1_out : 8'bz;  // Controlled_Buffer controlled_buffer_4
  assign controlled_buffer_1_out = and_3_out ? bit_extender_2_out : 8'bz;  // Controlled_Buffer controlled_buffer_5
  assign controlled_buffer_1_out = and_4_out ? bit_extender_3_out : 8'bz;  // Controlled_Buffer controlled_buffer_6
  or or_1 (or_1_out, and_2_out, and_3_out, and_4_out, and_5_out);
  assign bit_extender_1_out = {{7{1'b0}}, isVyActive};  // Bit_Extender bit_extender_1
  assign bit_extender_2_out = {{7{1'b0}}, Vy};  // Bit_Extender bit_extender_2
  assign bit_extender_3_out = {{7{1'b0}}, Vx};  // Bit_Extender bit_extender_3
  assign bit_extender_4_out = {{3{1'b0}}, ballY};  // Bit_Extender bit_extender_4
  ROM rom_1 (.addr(cdm_8_mark5_1_p14), .data(controlled_buffer_1_out), .sel(code));
  // Probe on controlled_buffer_1_out
  RAM ram_1 (
    .addr(cdm_8_mark5_1_p14), .data(controlled_buffer_1_out), .sel(and_6_out), .clk(Cl), .ld(rd_wr_prime));  // open: clr
  and and_7 (and_7_out, comparator_5_eq, ~rd_wr_prime, data);  // AND_Gate
  Comparator comparator_5 (.a(cdm_8_mark5_1_p14), .b(8'hf0), .eq(comparator_5_eq));  // open: gt, lt
  Pull_Resistor pull_resistor_1 (.node(code));
  Pull_Resistor pull_resistor_2 (.node(data));
  Register register_1 (.D(controlled_buffer_1_out), .en(and_7_out), .Q(register_1_q), .clk(clock_2_out));  // open: clr
  Clock clock_2 (.out(clock_2_out));
  Bit_Extender #(.out_width(5)) bit_extender_5 (.in(register_1_q), .out(bit_extender_5_out));
  // Probe on bit_extender_5_out
  RandBatPos randbatpos_1 (.BatPos(bit_extender_5_out), .RandBatPos(randbatpos_1_randbatpos));
  Register #(.width(5)) register_2 (
    .D(randbatpos_1_randbatpos), .Q(register_2_q), .clk(register_3_q), .clr(kinematic_controller_1_gol));  // open: en
  Register #(.width(1)) register_3 (.D(and_7_out), .Q(register_3_q), .clk(not_2_out));  // open: en, clr
  not not_2 (not_2_out, clock_2_out);
  not not_3 (Vy, kinematic_controller_1_vy);
  Hex_Digit_Display hex_digit_display_1 (.value(n10_1__10));  // open: dp
  Joystick #(.bits(5)) joystick_1 (.y(joystick_1_y));  // open: x
  // Probe on register_2_q
  and and_8 (and_8_out, and_7_out, clock_3_out);
  Clock #(.highDuration(256), .lowDuration(256)) clock_3 (.out(clock_3_out));
  Hex_Digit_Display hex_digit_display_2 (.value(n10_1__1));  // open: dp
  _10 u_10_1 (.Score(L), ._10(n10_1__10), ._1(n10_1__1));
  Button u_R (.out(R_out));
  DotMatrix #(.matrixcols(32), .matrixrows(32)) dotmatrix_1 (
    .col0(chipset_1_bus_0), .col1(chipset_1_bus_0_2), .col2(chipset_1_bus_0_3), .col3(chipset_1_bus_0_4),
    .col4(chipset_1_bus_0_5), .col5(chipset_1_bus_0_6), .col6(chipset_1_bus_0_7), .col7(chipset_1_bus_0_8),
    .col8(chipset_1_bus_0_9), .col9(chipset_1_bus_0_10), .col10(chipset_1_bus_0_11),
    .col11(chipset_1_bus_0_12), .col12(chipset_1_bus_0_13), .col13(chipset_1_bus_0_14),
    .col14(chipset_1_bus_0_15), .col15(chipset_1_bus_0_16), .col16(chipset_1_bus_0_17),
    .col17(chipset_1_bus_0_18), .col18(chipset_1_bus_0_19), .col19(chipset_1_bus_0_20),
    .col20(chipset_1_bus_0_21), .col21(chipset_1_bus_0_22), .col22(chipset_1_bus_0_23),
    .col23(chipset_1_bus_0_24), .col24(chipset_1_bus_0_25), .col25(chipset_1_bus_0_26),
    .col26(chipset_1_bus_0_27), .col27(chipset_1_bus_0_28), .col28(chipset_1_bus_0_29),
    .col29(chipset_1_bus_0_30), .col30(chipset_1_bus_0_31), .col31(chipset_1_bus_0_32));
  chipset chipset_1 (
    .chipID(kinematic_controller_1_chipid), .ballX(kinematic_controller_1_ballx),
    .ballY(kinematic_controller_1_bally), .leftbatY(kinematic_controller_1_leftbaty),
    .rightbatY(kinematic_controller_1_rightbaty), .bus_0(chipset_1_bus_0), .bus_0_2(chipset_1_bus_0_2),
    .bus_0_3(chipset_1_bus_0_3), .bus_0_4(chipset_1_bus_0_4), .bus_0_5(chipset_1_bus_0_5),
    .bus_0_6(chipset_1_bus_0_6), .bus_0_7(chipset_1_bus_0_7), .bus_0_8(chipset_1_bus_0_8),
    .bus_0_9(chipset_1_bus_0_9), .bus_0_10(chipset_1_bus_0_10), .bus_0_11(chipset_1_bus_0_11),
    .bus_0_12(chipset_1_bus_0_12), .bus_0_13(chipset_1_bus_0_13), .bus_0_14(chipset_1_bus_0_14),
    .bus_0_15(chipset_1_bus_0_15), .bus_0_16(chipset_1_bus_0_16), .bus_0_17(chipset_1_bus_0_17),
    .bus_0_18(chipset_1_bus_0_18), .bus_0_19(chipset_1_bus_0_19), .bus_0_20(chipset_1_bus_0_20),
    .bus_0_21(chipset_1_bus_0_21), .bus_0_22(chipset_1_bus_0_22), .bus_0_23(chipset_1_bus_0_23),
    .bus_0_24(chipset_1_bus_0_24), .bus_0_25(chipset_1_bus_0_25), .bus_0_26(chipset_1_bus_0_26),
    .bus_0_27(chipset_1_bus_0_27), .bus_0_28(chipset_1_bus_0_28), .bus_0_29(chipset_1_bus_0_29),
    .bus_0_30(chipset_1_bus_0_30), .bus_0_31(chipset_1_bus_0_31), .bus_0_32(chipset_1_bus_0_32));
  kinematic_controller kinematic_controller_1 (
    .reset(R_out), .joystick(joystick_1_y), .chipID(kinematic_controller_1_chipid),
    .ballX(kinematic_controller_1_ballx), .ballY(kinematic_controller_1_bally),
    .leftbatY(kinematic_controller_1_leftbaty), .leftScore(L), .rightScore(R), .ballY_2(ballY),
    .isVyActive(isVyActive), .Vy(kinematic_controller_1_vy), .Vx(Vx), .Collision(Collision), .tact(or_2_out),
    .rightbatY(kinematic_controller_1_rightbaty), .gol(kinematic_controller_1_gol),
    .rightbatYWanted(register_2_q), .rightBatStop(register_3_q));
  or or_2 (or_2_out, and_8_out, and_10_out, and_9_out);
  and and_9 (and_9_out, ~Collision, clock_4_out);  // AND_Gate
  and and_10 (and_10_out, Collision, and_7_out);
  Clock #(.highDuration(256), .lowDuration(256)) clock_4 (.out(clock_4_out));
  Hex_Digit_Display hex_digit_display_3 (.value(n10_2__10));  // open: dp
  Hex_Digit_Display hex_digit_display_4 (.value(n10_2__1));  // open: dp
  _10 u_10_2 (.Score(R), ._10(n10_2__10), ._1(n10_2__1));

  // Notes on the sheet:
  //   contents of rom_1 (hex, n*v repeats v):
  //   d0 1 b1 d0 4 b2 d0 0 71 e1 f ee 4f ee 4f c2 d0 2 b1 d3 0 7d e1 1c d1 ff ee 1e d1 1 d0 3 b2 d3 3 d0
  //   1a 7c ea 4e c4 1b c2 d2 0 76 ea 3e d2 0 72 ec 39 85 14 ee 3c c1 14 c5 ee 48 d2 1f 72 ea 46 14 ee 48
  //   85 14 c6 c0 d0 1a ee 25 c6 d0 f0 a2 ee 0 d4
  //   Register contains next ball position
endmodule

module chip (
  input  [4:0] chipID,
  input  [4:0] ballX,
  input  [4:0] ballY,
  input  [4:0] leftbatY,
  input  [4:0] rightbatY,
  output [31:0] chipOUT,
  output [4:0] chipID_1,
  output [4:0] ballX_unchanged,
  output [4:0] ballY_unchanged,
  output [4:0] leftbatY_unchanged,
  output [4:0] rightbatY_unchanged
);

  wire comparator_1_eq, comparator_2_eq, comparator_3_eq;
  wire [31:0] adder_1_out, adder_2_out, adder_3_out, adder_4_out, adder_5_out, multiplexer_1_out,
       multiplexer_2_out, multiplexer_3_out, shifter_1_out, shifter_2_out, shifter_3_out, shifter_4_out,
       shifter_5_out, shifter_6_out, shifter_7_out;

  Shifter #(.width(32)) shifter_1 (.in(32'h1), .\dist (rightbatY), .out(shifter_1_out));
  Shifter #(.width(32)) shifter_2 (.in(shifter_3_out), .\dist (5'b00001), .out(shifter_2_out));
  Shifter #(.width(32)) shifter_3 (.in(32'h1), .\dist (leftbatY), .out(shifter_3_out));
  Shifter #(.width(32)) shifter_4 (.in(shifter_1_out), .\dist (5'b00010), .out(shifter_4_out));
  Shifter #(.width(32)) shifter_5 (.in(shifter_1_out), .\dist (5'b00001), .out(shifter_5_out));
  Adder #(.width(32)) adder_1 (.a(shifter_5_out), .b(shifter_1_out), .out(adder_1_out));  // open: cin, cout
  Comparator #(.width(5)) comparator_1 (.a(chipID), .b(5'b00011), .eq(comparator_1_eq));  // open: gt, lt
  Shifter #(.width(32)) shifter_6 (.in(shifter_3_out), .\dist (5'b00010), .out(shifter_6_out));
  Adder #(.width(32)) adder_2 (.a(shifter_2_out), .b(shifter_3_out), .out(adder_2_out));  // open: cin, cout
  Comparator #(.width(5)) comparator_2 (.a(chipID), .b(ballX), .eq(comparator_2_eq));  // open: gt, lt
  Shifter #(.width(32)) shifter_7 (.in(32'h1), .\dist (ballY), .out(shifter_7_out));
  Comparator #(.width(5)) comparator_3 (.a(chipID), .b(5'b11100), .eq(comparator_3_eq));  // open: gt, lt
  Adder #(.width(32)) adder_3 (.a(shifter_4_out), .b(adder_1_out), .out(adder_3_out));  // open: cin, cout
  Adder #(.width(32)) adder_4 (.a(shifter_6_out), .b(adder_2_out), .out(adder_4_out));  // open: cin, cout
  Multiplexer #(.width(32)) multiplexer_1 (
    .in0({32{1'b0}}), .in1(shifter_7_out), .out(multiplexer_1_out), .sel(comparator_2_eq), .en(1'b1));
  Multiplexer #(.width(32)) multiplexer_2 (
    .in0({32{1'b0}}), .in1(adder_3_out), .out(multiplexer_2_out), .sel(comparator_3_eq), .en(1'b1));
  Multiplexer #(.width(32)) multiplexer_3 (
    .in0({32{1'b0}}), .in1(adder_4_out), .out(multiplexer_3_out), .sel(comparator_1_eq), .en(1'b1));
  Adder #(.width(32)) adder_5 (.a(multiplexer_3_out), .b(multiplexer_1_out), .out(adder_5_out));  // open: cin, cout
  Adder #(.width(32)) adder_6 (.a(adder_5_out), .b(multiplexer_2_out), .out(chipOUT));  // open: cin, cout
  Adder #(.width(5)) adder_7 (.a(chipID), .b(5'b00001), .out(chipID_1));  // open: cin, cout

  assign ballX_unchanged = ballX;
  assign ballY_unchanged = ballY;
  assign leftbatY_unchanged = leftbatY;
  assign rightbatY_unchanged = rightbatY;

  // Other names for the same wires on the sheet: bX[4:0] = ballX; bY[4:0] = ballY; ID[4:0] = chipID;
  //   lbtY[4:0] = leftbatY; rbtY[4:0] = rightbatY
endmodule

module chipset (
  input  [4:0] chipID,
  input  [4:0] ballX,
  input  [4:0] ballY,
  input  [4:0] leftbatY,
  input  [4:0] rightbatY,
  output [31:0] bus_0,
  output [31:0] bus_0_2,
  output [31:0] bus_0_3,
  output [31:0] bus_0_4,
  output [31:0] bus_0_5,
  output [31:0] bus_0_6,
  output [31:0] bus_0_7,
  output [31:0] bus_0_8,
  output [31:0] bus_0_9,
  output [31:0] bus_0_10,
  output [31:0] bus_0_11,
  output [31:0] bus_0_12,
  output [31:0] bus_0_13,
  output [31:0] bus_0_14,
  output [31:0] bus_0_15,
  output [31:0] bus_0_16,
  output [31:0] bus_0_17,
  output [31:0] bus_0_18,
  output [31:0] bus_0_19,
  output [31:0] bus_0_20,
  output [31:0] bus_0_21,
  output [31:0] bus_0_22,
  output [31:0] bus_0_23,
  output [31:0] bus_0_24,
  output [31:0] bus_0_25,
  output [31:0] bus_0_26,
  output [31:0] bus_0_27,
  output [31:0] bus_0_28,
  output [31:0] bus_0_29,
  output [31:0] bus_0_30,
  output [31:0] bus_0_31,
  output [31:0] bus_0_32
);

  wire [4:0] chip_1_ballx_unchanged, chip_1_bally_unchanged, chip_1_chipid_1, chip_1_leftbaty_unchanged,
       chip_1_rightbaty_unchanged, chip_2_ballx_unchanged, chip_2_bally_unchanged, chip_2_chipid_1,
       chip_2_leftbaty_unchanged, chip_2_rightbaty_unchanged, chip_3_ballx_unchanged, chip_3_bally_unchanged,
       chip_3_chipid_1, chip_3_leftbaty_unchanged, chip_3_rightbaty_unchanged, chip_4_ballx_unchanged,
       chip_4_bally_unchanged, chip_4_chipid_1, chip_4_leftbaty_unchanged, chip_4_rightbaty_unchanged,
       chip_5_ballx_unchanged, chip_5_bally_unchanged, chip_5_chipid_1, chip_5_leftbaty_unchanged,
       chip_5_rightbaty_unchanged, chip_6_ballx_unchanged, chip_6_bally_unchanged, chip_6_chipid_1,
       chip_6_leftbaty_unchanged, chip_6_rightbaty_unchanged, chip_7_ballx_unchanged, chip_7_bally_unchanged,
       chip_7_chipid_1, chip_7_leftbaty_unchanged, chip_7_rightbaty_unchanged, chip_8_ballx_unchanged,
       chip_8_bally_unchanged, chip_8_chipid_1, chip_8_leftbaty_unchanged, chip_8_rightbaty_unchanged,
       chip_9_ballx_unchanged, chip_9_bally_unchanged, chip_9_chipid_1, chip_9_leftbaty_unchanged,
       chip_9_rightbaty_unchanged, chip_10_ballx_unchanged, chip_10_bally_unchanged, chip_10_chipid_1,
       chip_10_leftbaty_unchanged, chip_10_rightbaty_unchanged, chip_11_ballx_unchanged,
       chip_11_bally_unchanged, chip_11_chipid_1, chip_11_leftbaty_unchanged, chip_11_rightbaty_unchanged,
       chip_12_ballx_unchanged, chip_12_bally_unchanged, chip_12_chipid_1, chip_12_leftbaty_unchanged,
       chip_12_rightbaty_unchanged, chip_13_ballx_unchanged, chip_13_bally_unchanged, chip_13_chipid_1,
       chip_13_leftbaty_unchanged, chip_13_rightbaty_unchanged, chip_14_ballx_unchanged,
       chip_14_bally_unchanged, chip_14_chipid_1, chip_14_leftbaty_unchanged, chip_14_rightbaty_unchanged,
       chip_15_ballx_unchanged, chip_15_bally_unchanged, chip_15_chipid_1, chip_15_leftbaty_unchanged,
       chip_15_rightbaty_unchanged, chip_16_ballx_unchanged, chip_16_bally_unchanged, chip_16_chipid_1,
       chip_16_leftbaty_unchanged, chip_16_rightbaty_unchanged, chip_17_ballx_unchanged,
       chip_17_bally_unchanged, chip_17_chipid_1, chip_17_leftbaty_unchanged, chip_17_rightbaty_unchanged,
       chip_18_ballx_unchanged, chip_18_bally_unchanged, chip_18_chipid_1, chip_18_leftbaty_unchanged,
       chip_18_rightbaty_unchanged, chip_19_ballx_unchanged, chip_19_bally_unchanged, chip_19_chipid_1,
       chip_19_leftbaty_unchanged, chip_19_rightbaty_unchanged, chip_20_ballx_unchanged,
       chip_20_bally_unchanged, chip_20_chipid_1, chip_20_leftbaty_unchanged, chip_20_rightbaty_unchanged,
       chip_21_ballx_unchanged, chip_21_bally_unchanged, chip_21_chipid_1, chip_21_leftbaty_unchanged,
       chip_21_rightbaty_unchanged, chip_22_ballx_unchanged, chip_22_bally_unchanged, chip_22_chipid_1,
       chip_22_leftbaty_unchanged, chip_22_rightbaty_unchanged, chip_23_ballx_unchanged,
       chip_23_bally_unchanged, chip_23_chipid_1, chip_23_leftbaty_unchanged, chip_23_rightbaty_unchanged,
       chip_24_ballx_unchanged, chip_24_bally_unchanged, chip_24_chipid_1, chip_24_leftbaty_unchanged,
       chip_24_rightbaty_unchanged, chip_25_ballx_unchanged, chip_25_bally_unchanged, chip_25_chipid_1,
       chip_25_leftbaty_unchanged, chip_25_rightbaty_unchanged, chip_26_ballx_unchanged,
       chip_26_bally_unchanged, chip_26_chipid_1, chip_26_leftbaty_unchanged, chip_26_rightbaty_unchanged,
       chip_27_ballx_unchanged, chip_27_bally_unchanged, chip_27_chipid_1, chip_27_leftbaty_unchanged,
       chip_27_rightbaty_unchanged, chip_28_ballx_unchanged, chip_28_bally_unchanged, chip_28_chipid_1,
       chip_28_leftbaty_unchanged, chip_28_rightbaty_unchanged, chip_29_ballx_unchanged,
       chip_29_bally_unchanged, chip_29_chipid_1, chip_29_leftbaty_unchanged, chip_29_rightbaty_unchanged,
       chip_30_ballx_unchanged, chip_30_bally_unchanged, chip_30_chipid_1, chip_30_leftbaty_unchanged,
       chip_30_rightbaty_unchanged, chip_32_ballx_unchanged, chip_32_bally_unchanged, chip_32_chipid_1,
       chip_32_leftbaty_unchanged, chip_32_rightbaty_unchanged;

  chip chip_1 (
    .chipID(chipID), .ballX(ballX), .ballY(ballY), .leftbatY(leftbatY), .rightbatY(rightbatY),
    .chipOUT(bus_0), .chipID_1(chip_1_chipid_1), .ballX_unchanged(chip_1_ballx_unchanged),
    .ballY_unchanged(chip_1_bally_unchanged), .leftbatY_unchanged(chip_1_leftbaty_unchanged),
    .rightbatY_unchanged(chip_1_rightbaty_unchanged));
  chip chip_2 (
    .chipID(chip_1_chipid_1), .ballX(chip_1_ballx_unchanged), .ballY(chip_1_bally_unchanged),
    .leftbatY(chip_1_leftbaty_unchanged), .rightbatY(chip_1_rightbaty_unchanged), .chipOUT(bus_0_2),
    .chipID_1(chip_2_chipid_1), .ballX_unchanged(chip_2_ballx_unchanged),
    .ballY_unchanged(chip_2_bally_unchanged), .leftbatY_unchanged(chip_2_leftbaty_unchanged),
    .rightbatY_unchanged(chip_2_rightbaty_unchanged));
  chip chip_3 (
    .chipID(chip_4_chipid_1), .ballX(chip_4_ballx_unchanged), .ballY(chip_4_bally_unchanged),
    .leftbatY(chip_4_leftbaty_unchanged), .rightbatY(chip_4_rightbaty_unchanged), .chipOUT(bus_0_5),
    .chipID_1(chip_3_chipid_1), .ballX_unchanged(chip_3_ballx_unchanged),
    .ballY_unchanged(chip_3_bally_unchanged), .leftbatY_unchanged(chip_3_leftbaty_unchanged),
    .rightbatY_unchanged(chip_3_rightbaty_unchanged));
  chip chip_4 (
    .chipID(chip_5_chipid_1), .ballX(chip_5_ballx_unchanged), .ballY(chip_5_bally_unchanged),
    .leftbatY(chip_5_leftbaty_unchanged), .rightbatY(chip_5_rightbaty_unchanged), .chipOUT(bus_0_4),
    .chipID_1(chip_4_chipid_1), .ballX_unchanged(chip_4_ballx_unchanged),
    .ballY_unchanged(chip_4_bally_unchanged), .leftbatY_unchanged(chip_4_leftbaty_unchanged),
    .rightbatY_unchanged(chip_4_rightbaty_unchanged));
  chip chip_5 (
    .chipID(chip_2_chipid_1), .ballX(chip_2_ballx_unchanged), .ballY(chip_2_bally_unchanged),
    .leftbatY(chip_2_leftbaty_unchanged), .rightbatY(chip_2_rightbaty_unchanged), .chipOUT(bus_0_3),
    .chipID_1(chip_5_chipid_1), .ballX_unchanged(chip_5_ballx_unchanged),
    .ballY_unchanged(chip_5_bally_unchanged), .leftbatY_unchanged(chip_5_leftbaty_unchanged),
    .rightbatY_unchanged(chip_5_rightbaty_unchanged));
  chip chip_6 (
    .chipID(chip_9_chipid_1), .ballX(chip_9_ballx_unchanged), .ballY(chip_9_bally_unchanged),
    .leftbatY(chip_9_leftbaty_unchanged), .rightbatY(chip_9_rightbaty_unchanged), .chipOUT(bus_0_9),
    .chipID_1(chip_6_chipid_1), .ballX_unchanged(chip_6_ballx_unchanged),
    .ballY_unchanged(chip_6_bally_unchanged), .leftbatY_unchanged(chip_6_leftbaty_unchanged),
    .rightbatY_unchanged(chip_6_rightbaty_unchanged));
  chip chip_7 (
    .chipID(chip_8_chipid_1), .ballX(chip_8_ballx_unchanged), .ballY(chip_8_bally_unchanged),
    .leftbatY(chip_8_leftbaty_unchanged), .rightbatY(chip_8_rightbaty_unchanged), .chipOUT(bus_0_7),
    .chipID_1(chip_7_chipid_1), .ballX_unchanged(chip_7_ballx_unchanged),
    .ballY_unchanged(chip_7_bally_unchanged), .leftbatY_unchanged(chip_7_leftbaty_unchanged),
    .rightbatY_unchanged(chip_7_rightbaty_unchanged));
  chip chip_8 (
    .chipID(chip_3_chipid_1), .ballX(chip_3_ballx_unchanged), .ballY(chip_3_bally_unchanged),
    .leftbatY(chip_3_leftbaty_unchanged), .rightbatY(chip_3_rightbaty_unchanged), .chipOUT(bus_0_6),
    .chipID_1(chip_8_chipid_1), .ballX_unchanged(chip_8_ballx_unchanged),
    .ballY_unchanged(chip_8_bally_unchanged), .leftbatY_unchanged(chip_8_leftbaty_unchanged),
    .rightbatY_unchanged(chip_8_rightbaty_unchanged));
  chip chip_9 (
    .chipID(chip_7_chipid_1), .ballX(chip_7_ballx_unchanged), .ballY(chip_7_bally_unchanged),
    .leftbatY(chip_7_leftbaty_unchanged), .rightbatY(chip_7_rightbaty_unchanged), .chipOUT(bus_0_8),
    .chipID_1(chip_9_chipid_1), .ballX_unchanged(chip_9_ballx_unchanged),
    .ballY_unchanged(chip_9_bally_unchanged), .leftbatY_unchanged(chip_9_leftbaty_unchanged),
    .rightbatY_unchanged(chip_9_rightbaty_unchanged));
  chip chip_10 (
    .chipID(chip_12_chipid_1), .ballX(chip_12_ballx_unchanged), .ballY(chip_12_bally_unchanged),
    .leftbatY(chip_12_leftbaty_unchanged), .rightbatY(chip_12_rightbaty_unchanged), .chipOUT(bus_0_13),
    .chipID_1(chip_10_chipid_1), .ballX_unchanged(chip_10_ballx_unchanged),
    .ballY_unchanged(chip_10_bally_unchanged), .leftbatY_unchanged(chip_10_leftbaty_unchanged),
    .rightbatY_unchanged(chip_10_rightbaty_unchanged));
  chip chip_11 (
    .chipID(chip_13_chipid_1), .ballX(chip_13_ballx_unchanged), .ballY(chip_13_bally_unchanged),
    .leftbatY(chip_13_leftbaty_unchanged), .rightbatY(chip_13_rightbaty_unchanged), .chipOUT(bus_0_11),
    .chipID_1(chip_11_chipid_1), .ballX_unchanged(chip_11_ballx_unchanged),
    .ballY_unchanged(chip_11_bally_unchanged), .leftbatY_unchanged(chip_11_leftbaty_unchanged),
    .rightbatY_unchanged(chip_11_rightbaty_unchanged));
  chip chip_12 (
    .chipID(chip_11_chipid_1), .ballX(chip_11_ballx_unchanged), .ballY(chip_11_bally_unchanged),
    .leftbatY(chip_11_leftbaty_unchanged), .rightbatY(chip_11_rightbaty_unchanged), .chipOUT(bus_0_12),
    .chipID_1(chip_12_chipid_1), .ballX_unchanged(chip_12_ballx_unchanged),
    .ballY_unchanged(chip_12_bally_unchanged), .leftbatY_unchanged(chip_12_leftbaty_unchanged),
    .rightbatY_unchanged(chip_12_rightbaty_unchanged));
  chip chip_13 (
    .chipID(chip_6_chipid_1), .ballX(chip_6_ballx_unchanged), .ballY(chip_6_bally_unchanged),
    .leftbatY(chip_6_leftbaty_unchanged), .rightbatY(chip_6_rightbaty_unchanged), .chipOUT(bus_0_10),
    .chipID_1(chip_13_chipid_1), .ballX_unchanged(chip_13_ballx_unchanged),
    .ballY_unchanged(chip_13_bally_unchanged), .leftbatY_unchanged(chip_13_leftbaty_unchanged),
    .rightbatY_unchanged(chip_13_rightbaty_unchanged));
  chip chip_14 (
    .chipID(chip_15_chipid_1), .ballX(chip_15_ballx_unchanged), .ballY(chip_15_bally_unchanged),
    .leftbatY(chip_15_leftbaty_unchanged), .rightbatY(chip_15_rightbaty_unchanged), .chipOUT(bus_0_16),
    .chipID_1(chip_14_chipid_1), .ballX_unchanged(chip_14_ballx_unchanged),
    .ballY_unchanged(chip_14_bally_unchanged), .leftbatY_unchanged(chip_14_leftbaty_unchanged),
    .rightbatY_unchanged(chip_14_rightbaty_unchanged));
  chip chip_15 (
    .chipID(chip_16_chipid_1), .ballX(chip_16_ballx_unchanged), .ballY(chip_16_bally_unchanged),
    .leftbatY(chip_16_leftbaty_unchanged), .rightbatY(chip_16_rightbaty_unchanged), .chipOUT(bus_0_15),
    .chipID_1(chip_15_chipid_1), .ballX_unchanged(chip_15_ballx_unchanged),
    .ballY_unchanged(chip_15_bally_unchanged), .leftbatY_unchanged(chip_15_leftbaty_unchanged),
    .rightbatY_unchanged(chip_15_rightbaty_unchanged));
  chip chip_16 (
    .chipID(chip_10_chipid_1), .ballX(chip_10_ballx_unchanged), .ballY(chip_10_bally_unchanged),
    .leftbatY(chip_10_leftbaty_unchanged), .rightbatY(chip_10_rightbaty_unchanged), .chipOUT(bus_0_14),
    .chipID_1(chip_16_chipid_1), .ballX_unchanged(chip_16_ballx_unchanged),
    .ballY_unchanged(chip_16_bally_unchanged), .leftbatY_unchanged(chip_16_leftbaty_unchanged),
    .rightbatY_unchanged(chip_16_rightbaty_unchanged));
  chip chip_17 (
    .chipID(chip_14_chipid_1), .ballX(chip_14_ballx_unchanged), .ballY(chip_14_bally_unchanged),
    .leftbatY(chip_14_leftbaty_unchanged), .rightbatY(chip_14_rightbaty_unchanged), .chipOUT(bus_0_17),
    .chipID_1(chip_17_chipid_1), .ballX_unchanged(chip_17_ballx_unchanged),
    .ballY_unchanged(chip_17_bally_unchanged), .leftbatY_unchanged(chip_17_leftbaty_unchanged),
    .rightbatY_unchanged(chip_17_rightbaty_unchanged));
  chip chip_18 (
    .chipID(chip_19_chipid_1), .ballX(chip_19_ballx_unchanged), .ballY(chip_19_bally_unchanged),
    .leftbatY(chip_19_leftbaty_unchanged), .rightbatY(chip_19_rightbaty_unchanged), .chipOUT(bus_0_21),
    .chipID_1(chip_18_chipid_1), .ballX_unchanged(chip_18_ballx_unchanged),
    .ballY_unchanged(chip_18_bally_unchanged), .leftbatY_unchanged(chip_18_leftbaty_unchanged),
    .rightbatY_unchanged(chip_18_rightbaty_unchanged));
  chip chip_19 (
    .chipID(chip_20_chipid_1), .ballX(chip_20_ballx_unchanged), .ballY(chip_20_bally_unchanged),
    .leftbatY(chip_20_leftbaty_unchanged), .rightbatY(chip_20_rightbaty_unchanged), .chipOUT(bus_0_20),
    .chipID_1(chip_19_chipid_1), .ballX_unchanged(chip_19_ballx_unchanged),
    .ballY_unchanged(chip_19_bally_unchanged), .leftbatY_unchanged(chip_19_leftbaty_unchanged),
    .rightbatY_unchanged(chip_19_rightbaty_unchanged));
  chip chip_20 (
    .chipID(chip_21_chipid_1), .ballX(chip_21_ballx_unchanged), .ballY(chip_21_bally_unchanged),
    .leftbatY(chip_21_leftbaty_unchanged), .rightbatY(chip_21_rightbaty_unchanged), .chipOUT(bus_0_19),
    .chipID_1(chip_20_chipid_1), .ballX_unchanged(chip_20_ballx_unchanged),
    .ballY_unchanged(chip_20_bally_unchanged), .leftbatY_unchanged(chip_20_leftbaty_unchanged),
    .rightbatY_unchanged(chip_20_rightbaty_unchanged));
  chip chip_21 (
    .chipID(chip_17_chipid_1), .ballX(chip_17_ballx_unchanged), .ballY(chip_17_bally_unchanged),
    .leftbatY(chip_17_leftbaty_unchanged), .rightbatY(chip_17_rightbaty_unchanged), .chipOUT(bus_0_18),
    .chipID_1(chip_21_chipid_1), .ballX_unchanged(chip_21_ballx_unchanged),
    .ballY_unchanged(chip_21_bally_unchanged), .leftbatY_unchanged(chip_21_leftbaty_unchanged),
    .rightbatY_unchanged(chip_21_rightbaty_unchanged));
  chip chip_22 (
    .chipID(chip_25_chipid_1), .ballX(chip_25_ballx_unchanged), .ballY(chip_25_bally_unchanged),
    .leftbatY(chip_25_leftbaty_unchanged), .rightbatY(chip_25_rightbaty_unchanged), .chipOUT(bus_0_24),
    .chipID_1(chip_22_chipid_1), .ballX_unchanged(chip_22_ballx_unchanged),
    .ballY_unchanged(chip_22_bally_unchanged), .leftbatY_unchanged(chip_22_leftbaty_unchanged),
    .rightbatY_unchanged(chip_22_rightbaty_unchanged));
  chip chip_23 (
    .chipID(chip_22_chipid_1), .ballX(chip_22_ballx_unchanged), .ballY(chip_22_bally_unchanged),
    .leftbatY(chip_22_leftbaty_unchanged), .rightbatY(chip_22_rightbaty_unchanged), .chipOUT(bus_0_25),
    .chipID_1(chip_23_chipid_1), .ballX_unchanged(chip_23_ballx_unchanged),
    .ballY_unchanged(chip_23_bally_unchanged), .leftbatY_unchanged(chip_23_leftbaty_unchanged),
    .rightbatY_unchanged(chip_23_rightbaty_unchanged));
  chip chip_24 (
    .chipID(chip_18_chipid_1), .ballX(chip_18_ballx_unchanged), .ballY(chip_18_bally_unchanged),
    .leftbatY(chip_18_leftbaty_unchanged), .rightbatY(chip_18_rightbaty_unchanged), .chipOUT(bus_0_22),
    .chipID_1(chip_24_chipid_1), .ballX_unchanged(chip_24_ballx_unchanged),
    .ballY_unchanged(chip_24_bally_unchanged), .leftbatY_unchanged(chip_24_leftbaty_unchanged),
    .rightbatY_unchanged(chip_24_rightbaty_unchanged));
  chip chip_25 (
    .chipID(chip_24_chipid_1), .ballX(chip_24_ballx_unchanged), .ballY(chip_24_bally_unchanged),
    .leftbatY(chip_24_leftbaty_unchanged), .rightbatY(chip_24_rightbaty_unchanged), .chipOUT(bus_0_23),
    .chipID_1(chip_25_chipid_1), .ballX_unchanged(chip_25_ballx_unchanged),
    .ballY_unchanged(chip_25_bally_unchanged), .leftbatY_unchanged(chip_25_leftbaty_unchanged),
    .rightbatY_unchanged(chip_25_rightbaty_unchanged));
  chip chip_26 (
    .chipID(chip_27_chipid_1), .ballX(chip_27_ballx_unchanged), .ballY(chip_27_bally_unchanged),
    .leftbatY(chip_27_leftbaty_unchanged), .rightbatY(chip_27_rightbaty_unchanged), .chipOUT(bus_0_28),
    .chipID_1(chip_26_chipid_1), .ballX_unchanged(chip_26_ballx_unchanged),
    .ballY_unchanged(chip_26_bally_unchanged), .leftbatY_unchanged(chip_26_leftbaty_unchanged),
    .rightbatY_unchanged(chip_26_rightbaty_unchanged));
  chip chip_27 (
    .chipID(chip_28_chipid_1), .ballX(chip_28_ballx_unchanged), .ballY(chip_28_bally_unchanged),
    .leftbatY(chip_28_leftbaty_unchanged), .rightbatY(chip_28_rightbaty_unchanged), .chipOUT(bus_0_27),
    .chipID_1(chip_27_chipid_1), .ballX_unchanged(chip_27_ballx_unchanged),
    .ballY_unchanged(chip_27_bally_unchanged), .leftbatY_unchanged(chip_27_leftbaty_unchanged),
    .rightbatY_unchanged(chip_27_rightbaty_unchanged));
  chip chip_28 (
    .chipID(chip_23_chipid_1), .ballX(chip_23_ballx_unchanged), .ballY(chip_23_bally_unchanged),
    .leftbatY(chip_23_leftbaty_unchanged), .rightbatY(chip_23_rightbaty_unchanged), .chipOUT(bus_0_26),
    .chipID_1(chip_28_chipid_1), .ballX_unchanged(chip_28_ballx_unchanged),
    .ballY_unchanged(chip_28_bally_unchanged), .leftbatY_unchanged(chip_28_leftbaty_unchanged),
    .rightbatY_unchanged(chip_28_rightbaty_unchanged));
  chip chip_29 (
    .chipID(chip_26_chipid_1), .ballX(chip_26_ballx_unchanged), .ballY(chip_26_bally_unchanged),
    .leftbatY(chip_26_leftbaty_unchanged), .rightbatY(chip_26_rightbaty_unchanged), .chipOUT(bus_0_29),
    .chipID_1(chip_29_chipid_1), .ballX_unchanged(chip_29_ballx_unchanged),
    .ballY_unchanged(chip_29_bally_unchanged), .leftbatY_unchanged(chip_29_leftbaty_unchanged),
    .rightbatY_unchanged(chip_29_rightbaty_unchanged));
  chip chip_30 (
    .chipID(chip_32_chipid_1), .ballX(chip_32_ballx_unchanged), .ballY(chip_32_bally_unchanged),
    .leftbatY(chip_32_leftbaty_unchanged), .rightbatY(chip_32_rightbaty_unchanged), .chipOUT(bus_0_31),
    .chipID_1(chip_30_chipid_1), .ballX_unchanged(chip_30_ballx_unchanged),
    .ballY_unchanged(chip_30_bally_unchanged), .leftbatY_unchanged(chip_30_leftbaty_unchanged),
    .rightbatY_unchanged(chip_30_rightbaty_unchanged));
  chip chip_31 (
    .chipID(chip_30_chipid_1), .ballX(chip_30_ballx_unchanged), .ballY(chip_30_bally_unchanged),
    .leftbatY(chip_30_leftbaty_unchanged), .rightbatY(chip_30_rightbaty_unchanged), .chipOUT(bus_0_32));  // open: chipID_1, ballX_unchanged, ballY_unchanged, leftbatY_unchanged, rightbatY_unchanged
  chip chip_32 (
    .chipID(chip_29_chipid_1), .ballX(chip_29_ballx_unchanged), .ballY(chip_29_bally_unchanged),
    .leftbatY(chip_29_leftbaty_unchanged), .rightbatY(chip_29_rightbaty_unchanged), .chipOUT(bus_0_30),
    .chipID_1(chip_32_chipid_1), .ballX_unchanged(chip_32_ballx_unchanged),
    .ballY_unchanged(chip_32_bally_unchanged), .leftbatY_unchanged(chip_32_leftbaty_unchanged),
    .rightbatY_unchanged(chip_32_rightbaty_unchanged));
endmodule

module leftbatControl (
  input  tact,
  input  reset,
  input  [4:0] joystick,
  output [4:0] leftbatY
);

  wire and_1_out, comparator_1_eq, comparator_2_eq, comparator_3_eq, comparator_4_lt, comparator_5_gt,
       comparator_6_eq, not_1_out;
  wire [4:0] adder_1_out, multiplexer_1_out, multiplexer_2_out, multiplexer_3_out, multiplexer_4_out,
       register_1_q, subtractor_1_out, subtractor_2_out;

  Comparator #(.width(5)) comparator_1 (.a(register_1_q), .b({5{1'b0}}), .eq(comparator_1_eq));  // open: gt, lt
  Multiplexer #(.width(5)) multiplexer_1 (
    .in0(register_1_q), .in1(5'b01111), .out(multiplexer_1_out), .sel(comparator_1_eq));  // open: en
  Comparator #(.width(5)) comparator_2 (.a(multiplexer_1_out), .b(5'b11110), .eq(comparator_2_eq));  // open: gt, lt
  Comparator #(.width(5)) comparator_3 (.a(multiplexer_1_out), .b(5'b00001), .eq(comparator_3_eq));  // open: gt, lt
  Adder #(.width(5)) adder_1 (.a(multiplexer_1_out), .b(multiplexer_2_out), .out(adder_1_out));  // open: cin, cout
  Multiplexer #(.width(5)) multiplexer_2 (
    .in0(5'b00001), .in1({5{1'b0}}), .out(multiplexer_2_out), .sel(comparator_2_eq));  // open: en
  Multiplexer #(.width(5)) multiplexer_3 (
    .in0(5'b00001), .in1({5{1'b0}}), .out(multiplexer_3_out), .sel(comparator_3_eq));  // open: en
  Subtractor #(.width(5)) subtractor_1 (
    .a(multiplexer_1_out), .b(multiplexer_3_out), .out(subtractor_1_out));  // open: bin, bout
  Comparator #(.width(5), .mode("unsigned")) comparator_4 (
    .a(5'b01001), .b(joystick), .lt(comparator_4_lt));  // open: gt, eq
  Comparator #(.width(5), .mode("unsigned")) comparator_5 (
    .a(5'b10111), .b(joystick), .gt(comparator_5_gt));  // open: eq, lt
  Multiplexer #(.width(5)) multiplexer_4 (
    .in0(adder_1_out), .in1(subtractor_1_out), .out(multiplexer_4_out), .sel(comparator_4_lt));  // open: en
  and and_1 (and_1_out, comparator_4_lt, comparator_5_gt);
  not not_1 (not_1_out, and_1_out);
  Register #(.width(5)) register_1 (.D(multiplexer_4_out), .en(not_1_out), .Q(register_1_q), .clk(tact), .clr(reset));
  Subtractor #(.width(5)) subtractor_2 (.a(register_1_q), .b(5'b00001), .out(subtractor_2_out));  // open: bin, bout
  Comparator #(.width(5), .mode("unsigned")) comparator_6 (
    .a(subtractor_2_out), .b({5{1'b1}}), .eq(comparator_6_eq));  // open: gt, lt
  Multiplexer #(.width(5)) multiplexer_5 (
    .in0(subtractor_2_out), .in1(5'b01110), .out(leftbatY), .sel(comparator_6_eq));  // open: en
endmodule

module kinematic_controller (
  input  reset,
  input  [4:0] joystick,
  input  tact,
  input  [4:0] rightbatYWanted,
  input  rightBatStop,
  output gol,
  output [6:0] leftScore,
  output [4:0] chipID,
  output [6:0] rightScore,
  output [4:0] ballX,
  output [4:0] ballY,
  output [4:0] ballY_2,
  output [4:0] leftbatY,
  output [4:0] rightbatY,
  output isVyActive,
  output Vy,
  output Vx,
  output Collision
);

  wire down, left, reset_t, right, rightbatywanted_1_down, rightbatywanted_1_up, up;

  rightbatYWanted rightbatywanted_1 (
    .rightbatY(rightbatY), .rightbatYWanted(rightbatYWanted), .rightBatStop(rightBatStop), .reset(reset_t),
    .ballX(ballX), .up(rightbatywanted_1_up), .down(rightbatywanted_1_down));
  or or_1 (reset_t, gol, reset);
  ballXYControl ballxycontrol_1 (.reset(reset_t), .down(left), .up(right), .leftbatY(ballX), .tact(tact));
  ballXYControl ballxycontrol_2 (.reset(reset_t), .down(down), .up(up), .leftbatY(ballY), .tact(tact));
  leftbatControl leftbatcontrol_1 (.reset(reset_t), .joystick(joystick), .leftbatY(leftbatY), .tact(tact));
  rightbatControl rightbatcontrol_1 (
    .reset(reset_t), .down(rightbatywanted_1_down), .up(rightbatywanted_1_up), .rightbatY(rightbatY));
  score score_1 (.leftScore(leftScore), .reset(gol), .Score_reset(reset), .rightScore(rightScore), .ballX(ballX));
  ballMover ballmover_1 (
    .reset(reset_t), .ballX(ballX), .ballY(ballY), .leftbatY(leftbatY), .rightbatY(rightbatY), .up(up),
    .left(left), .right(right), .down(down), .Vy(Vy), .isVyActive(isVyActive), .Vx(Vx), .Collision(Collision));

  assign ballY_2 = ballY;
  assign chipID = {5{1'b0}};

  // Other names for the same wires on the sheet: Sreset = reset
endmodule

module rightbatControl (
  input  reset,
  input  down,
  input  up,
  output [4:0] rightbatY
);

  wire clock_1_out, comparator_1_eq, comparator_2_eq, comparator_3_eq, comparator_4_eq, or_1_out;
  wire [4:0] adder_1_out, multiplexer_1_out, multiplexer_2_out, multiplexer_3_out, multiplexer_4_out,
       register_1_q, subtractor_1_out, subtractor_2_out;

  Comparator #(.width(5)) comparator_1 (.a(register_1_q), .b({5{1'b0}}), .eq(comparator_1_eq));  // open: gt, lt
  Multiplexer #(.width(5)) multiplexer_1 (
    .in0(register_1_q), .in1(5'b01111), .out(multiplexer_1_out), .sel(comparator_1_eq));  // open: en
  Comparator #(.width(5)) comparator_2 (.a(multiplexer_1_out), .b(5'b11110), .eq(comparator_2_eq));  // open: gt, lt
  Comparator #(.width(5)) comparator_3 (.a(multiplexer_1_out), .b(5'b00001), .eq(comparator_3_eq));  // open: gt, lt
  Adder #(.width(5)) adder_1 (.a(multiplexer_1_out), .b(multiplexer_2_out), .out(adder_1_out));  // open: cin, cout
  Multiplexer #(.width(5)) multiplexer_2 (
    .in0(5'b00001), .in1({5{1'b0}}), .out(multiplexer_2_out), .sel(comparator_2_eq));  // open: en
  Multiplexer #(.width(5)) multiplexer_3 (
    .in0(5'b00001), .in1({5{1'b0}}), .out(multiplexer_3_out), .sel(comparator_3_eq));  // open: en
  Subtractor #(.width(5)) subtractor_1 (
    .a(multiplexer_1_out), .b(multiplexer_3_out), .out(subtractor_1_out));  // open: bin, bout
  Multiplexer #(.width(5)) multiplexer_4 (
    .in0(adder_1_out), .in1(subtractor_1_out), .out(multiplexer_4_out), .sel(down));  // open: en
  or or_1 (or_1_out, down, up);
  Clock #(.highDuration(256), .lowDuration(256)) clock_1 (.out(clock_1_out));
  Register #(.width(5)) register_1 (
    .D(multiplexer_4_out), .en(or_1_out), .Q(register_1_q), .clk(clock_1_out), .clr(reset));
  Subtractor #(.width(5)) subtractor_2 (.a(register_1_q), .b(5'b00001), .out(subtractor_2_out));  // open: bin, bout
  Comparator #(.width(5), .mode("unsigned")) comparator_4 (
    .a(subtractor_2_out), .b({5{1'b1}}), .eq(comparator_4_eq));  // open: gt, lt
  Multiplexer #(.width(5)) multiplexer_5 (
    .in0(subtractor_2_out), .in1(5'b01110), .out(rightbatY), .sel(comparator_4_eq));  // open: en
endmodule

module ballXYControl (
  input  tact,
  input  reset,
  input  down,
  input  up,
  output [4:0] leftbatY
);

  wire comparator_1_eq, comparator_2_eq, comparator_3_eq, comparator_4_eq, or_1_out;
  wire [5:0] adder_1_out, multiplexer_1_out, multiplexer_2_out, multiplexer_3_out, multiplexer_4_out,
       register_1_q, subtractor_1_out, subtractor_2_out;
  wire [5:5] multiplexer_5_out;

  Comparator #(.width(6)) comparator_1 (.a(register_1_q), .b({6{1'b0}}), .eq(comparator_1_eq));  // open: gt, lt
  Multiplexer #(.width(6)) multiplexer_1 (
    .in0(register_1_q), .in1(6'b010000), .out(multiplexer_1_out), .sel(comparator_1_eq));  // open: en
  Comparator #(.width(6)) comparator_2 (.a(multiplexer_1_out), .b(6'b100000), .eq(comparator_2_eq));  // open: gt, lt
  Comparator #(.width(6)) comparator_3 (.a(multiplexer_1_out), .b(6'b000001), .eq(comparator_3_eq));  // open: gt, lt
  Adder #(.width(6)) adder_1 (.a(multiplexer_1_out), .b(multiplexer_2_out), .out(adder_1_out));  // open: cin, cout
  Multiplexer #(.width(6)) multiplexer_2 (
    .in0(6'b000001), .in1({6{1'b0}}), .out(multiplexer_2_out), .sel(comparator_2_eq));  // open: en
  Multiplexer #(.width(6)) multiplexer_3 (
    .in0(6'b000001), .in1({6{1'b0}}), .out(multiplexer_3_out), .sel(comparator_3_eq));  // open: en
  Subtractor #(.width(6)) subtractor_1 (
    .a(multiplexer_1_out), .b(multiplexer_3_out), .out(subtractor_1_out));  // open: bin, bout
  Multiplexer #(.width(6)) multiplexer_4 (
    .in0(adder_1_out), .in1(subtractor_1_out), .out(multiplexer_4_out), .sel(down));  // open: en
  or or_1 (or_1_out, down, up);
  Register #(.width(6)) register_1 (.D(multiplexer_4_out), .en(or_1_out), .Q(register_1_q), .clk(tact), .clr(reset));
  Subtractor #(.width(6)) subtractor_2 (.a(register_1_q), .b(6'b000001), .out(subtractor_2_out));  // open: bin, bout
  Comparator #(.width(6), .mode("unsigned")) comparator_4 (
    .a(subtractor_2_out), .b({6{1'b1}}), .eq(comparator_4_eq));  // open: gt, lt
  Multiplexer #(.width(6)) multiplexer_5 (
    .in0(subtractor_2_out), .in1(6'b001111), .out({multiplexer_5_out[5], leftbatY}), .sel(comparator_4_eq));  // open: en
endmodule

module score (
  input  [4:0] ballX,
  input  Score_reset,
  output [6:0] leftScore,
  output reset,
  output [6:0] rightScore
);

  wire and_1_out, and_2_out, clock_1_out, comparator_1_eq, comparator_2_eq, comparator_3_eq, comparator_4_eq,
       not_1_out, or_1_out;
  wire [6:0] adder_1_out, adder_2_out, multiplexer_1_out, multiplexer_2_out;

  Comparator #(.width(7), .mode("unsigned")) comparator_1 (
    .a(leftScore), .b(7'b1100011), .eq(comparator_1_eq));  // open: gt, lt
  Comparator #(.width(7), .mode("unsigned")) comparator_2 (
    .a(rightScore), .b(7'b1100011), .eq(comparator_2_eq));  // open: gt, lt
  Adder #(.width(7)) adder_1 (.a(leftScore), .b(multiplexer_1_out), .out(adder_1_out));  // open: cin, cout
  Multiplexer #(.width(7)) multiplexer_1 (
    .in0(7'b0000001), .in1({7{1'b0}}), .out(multiplexer_1_out), .sel(comparator_1_eq));  // open: en
  Comparator #(.width(5), .mode("unsigned")) comparator_3 (
    .a(ballX), .b({5{1'b1}}), .eq(comparator_3_eq));  // open: gt, lt
  Comparator #(.width(5), .mode("unsigned")) comparator_4 (
    .a(ballX), .b({5{1'b0}}), .eq(comparator_4_eq));  // open: gt, lt
  Adder #(.width(7)) adder_2 (.a(rightScore), .b(multiplexer_2_out), .out(adder_2_out));  // open: cin, cout
  Multiplexer #(.width(7)) multiplexer_2 (
    .in0(7'b0000001), .in1({7{1'b0}}), .out(multiplexer_2_out), .sel(comparator_2_eq));  // open: en
  Register #(.width(7)) register_1 (.D(adder_1_out), .en(1'b1), .Q(leftScore), .clk(and_1_out), .clr(Score_reset));
  and and_1 (and_1_out, comparator_3_eq, clock_1_out);
  Clock #(.highDuration(256), .lowDuration(256)) clock_1 (.out(clock_1_out));
  Register #(.width(7)) register_2 (.D(adder_2_out), .en(1'b1), .Q(rightScore), .clk(and_2_out), .clr(Score_reset));
  and and_2 (and_2_out, comparator_4_eq, clock_1_out);
  or or_1 (or_1_out, comparator_3_eq, comparator_4_eq);
  not not_1 (not_1_out, clock_1_out);
  and and_3 (reset, not_1_out, or_1_out);
endmodule

module _10 (
  input  [6:0] Score,
  output [3:0] _10,
  output [3:0] _1
);

  wire [6:4] divider_1_out, divider_1_rem;

  // Probe on Score
  Divider #(.width(7)) divider_1 (
    .a(Score), .b(7'b0001010), .out({divider_1_out, _10}), .rem({divider_1_rem, _1}));  // open: upper
  // Probe on _10
  // Probe on _1
endmodule

module ballMover (
  input  reset,
  input  [4:0] ballX,
  input  [4:0] ballY,
  input  [4:0] leftbatY,
  input  [4:0] rightbatY,
  output Vx,
  output up,
  output left,
  output right,
  output Collision,
  output down,
  output isVyActive,
  output Vy
);

  wire and_1_out, and_2_out, and_3_out, and_4_out, and_5_out, and_6_out, and_7_out, and_8_out, and_9_out,
       and_10_out, and_11_out, and_12_out, and_13_out, and_14_out, and_15_out, comparator_1_eq,
       comparator_2_eq, comparator_3_eq, comparator_4_eq, comparator_5_eq, comparator_6_eq, comparator_7_eq,
       comparator_8_eq, comparator_9_eq, comparator_10_eq, comparator_11_eq, comparator_12_eq,
       comparator_13_eq, comparator_14_eq, comparator_15_eq, comparator_16_eq, comparator_17_eq,
       comparator_18_eq, comparator_19_eq, comparator_20_eq, comparator_21_eq, comparator_22_eq,
       comparator_23_eq, not_1_out, not_2_out, not_3_out, not_4_out, not_6_out, or_1_out, or_2_out, or_3_out,
       or_4_out, or_5_out, or_6_out, or_7_out, or_8_out;
  wire [4:0] adder_1_out, adder_2_out, adder_3_out, adder_4_out, adder_5_out, adder_6_out, adder_7_out,
       adder_8_out;

  Adder #(.width(5)) adder_1 (.a(leftbatY), .b(5'b00001), .out(adder_1_out));  // open: cin, cout
  Adder #(.width(5)) adder_2 (.a(leftbatY), .b(5'b00010), .out(adder_2_out));  // open: cin, cout
  Adder #(.width(5)) adder_3 (.a(rightbatY), .b(5'b00010), .out(adder_3_out));  // open: cin, cout
  Adder #(.width(5)) adder_4 (.a(leftbatY), .b(5'b00001), .out(adder_4_out));  // open: cin, cout
  Adder #(.width(5)) adder_5 (.a(rightbatY), .b(5'b00001), .out(adder_5_out));  // open: cin, cout
  Comparator #(.width(5), .mode("unsigned")) comparator_1 (
    .a(ballX), .b(5'b00100), .eq(comparator_1_eq));  // open: gt, lt
  Comparator #(.width(5), .mode("unsigned")) comparator_2 (
    .a(ballY), .b(leftbatY), .eq(comparator_2_eq));  // open: gt, lt
  Comparator #(.width(5), .mode("unsigned")) comparator_3 (
    .a(ballY), .b(adder_1_out), .eq(comparator_3_eq));  // open: gt, lt
  Adder #(.width(5)) adder_6 (.a(leftbatY), .b(5'b00010), .out(adder_6_out));  // open: cin, cout
  Comparator #(.width(5), .mode("unsigned")) comparator_4 (
    .a(ballX), .b(5'b11011), .eq(comparator_4_eq));  // open: gt, lt
  Adder #(.width(5)) adder_7 (.a(rightbatY), .b(5'b00001), .out(adder_7_out));  // open: cin, cout
  Comparator #(.width(5), .mode("unsigned")) comparator_5 (
    .a(ballX), .b(5'b00100), .eq(comparator_5_eq));  // open: gt, lt
  Comparator #(.width(5), .mode("unsigned")) comparator_6 (
    .a(ballY), .b(leftbatY), .eq(comparator_6_eq));  // open: gt, lt
  Comparator #(.width(5), .mode("unsigned")) comparator_7 (
    .a(ballX), .b(5'b11011), .eq(comparator_7_eq));  // open: gt, lt
  Comparator #(.width(5), .mode("unsigned")) comparator_8 (
    .a(ballY), .b(rightbatY), .eq(comparator_8_eq));  // open: gt, lt
  Comparator #(.width(5), .mode("unsigned")) comparator_9 (
    .a(ballY), .b({5{1'b0}}), .eq(comparator_9_eq));  // open: gt, lt
  Comparator #(.width(5), .mode("unsigned")) comparator_10 (
    .a(ballX), .b(5'b00100), .eq(comparator_10_eq));  // open: gt, lt
  Comparator #(.width(5), .mode("unsigned")) comparator_11 (
    .a(ballY), .b(adder_2_out), .eq(comparator_11_eq));  // open: gt, lt
  Comparator #(.width(5), .mode("unsigned")) comparator_12 (
    .a(ballX), .b(5'b11011), .eq(comparator_12_eq));  // open: gt, lt
  Comparator #(.width(5), .mode("unsigned")) comparator_13 (
    .a(ballY), .b(adder_3_out), .eq(comparator_13_eq));  // open: gt, lt
  Comparator #(.width(5), .mode("unsigned")) comparator_14 (
    .a(ballY), .b({5{1'b1}}), .eq(comparator_14_eq));  // open: gt, lt
  Comparator #(.width(5), .mode("unsigned")) comparator_15 (
    .a(ballX), .b(5'b00100), .eq(comparator_15_eq));  // open: gt, lt
  Comparator #(.width(5), .mode("unsigned")) comparator_16 (
    .a(ballY), .b(adder_4_out), .eq(comparator_16_eq));  // open: gt, lt
  Comparator #(.width(5), .mode("unsigned")) comparator_17 (
    .a(ballX), .b(5'b11011), .eq(comparator_17_eq));  // open: gt, lt
  Comparator #(.width(5), .mode("unsigned")) comparator_18 (
    .a(ballY), .b(adder_5_out), .eq(comparator_18_eq));  // open: gt, lt
  and and_1 (and_1_out, comparator_1_eq, or_1_out);
  or or_1 (or_1_out, comparator_2_eq, comparator_3_eq, comparator_19_eq);
  Comparator #(.width(5), .mode("unsigned")) comparator_19 (
    .a(ballY), .b(adder_6_out), .eq(comparator_19_eq));  // open: gt, lt
  Comparator #(.width(5), .mode("unsigned")) comparator_20 (
    .a(ballY), .b(rightbatY), .eq(comparator_20_eq));  // open: gt, lt
  Comparator #(.width(5), .mode("unsigned")) comparator_21 (
    .a(ballY), .b(adder_7_out), .eq(comparator_21_eq));  // open: gt, lt
  Comparator #(.width(5), .mode("unsigned")) comparator_22 (
    .a(ballY), .b(adder_8_out), .eq(comparator_22_eq));  // open: gt, lt
  Adder #(.width(5)) adder_8 (.a(rightbatY), .b(5'b00010), .out(adder_8_out));  // open: cin, cout
  and and_2 (and_2_out, comparator_5_eq, comparator_6_eq);
  and and_3 (and_3_out, comparator_7_eq, comparator_8_eq);
  and and_4 (and_4_out, comparator_10_eq, comparator_11_eq);
  and and_5 (and_5_out, comparator_12_eq, comparator_13_eq);
  and and_6 (and_6_out, comparator_15_eq, comparator_16_eq);
  and and_7 (and_7_out, comparator_17_eq, comparator_18_eq);
  and and_8 (and_8_out, comparator_4_eq, or_2_out);
  or or_2 (or_2_out, comparator_20_eq, comparator_21_eq, comparator_22_eq);
  or or_3 (or_3_out, and_2_out, and_3_out);
  and and_9 (and_9_out, or_3_out, not_1_out);
  not not_1 (not_1_out, comparator_9_eq);
  or or_4 (or_4_out, and_6_out, and_7_out);
  or or_5 (or_5_out, and_1_out, and_8_out);
  or or_6 (or_6_out, and_4_out, and_5_out);
  and and_10 (and_10_out, or_6_out, not_2_out);
  not not_2 (not_2_out, comparator_14_eq);
  not not_3 (not_3_out, isVyActive);
  and and_11 (and_11_out, and_9_out, not_3_out);
  and and_12 (and_12_out, and_10_out, not_3_out);
  and and_13 (and_13_out, or_4_out, isVyActive);
  or or_7 (or_7_out, and_11_out, and_12_out, and_13_out);
  Vxy vxy_1 (.reset(reset), .change(or_7_out), .Vx(isVyActive));
  and and_14 (and_14_out, and_9_out, not_4_out);
  not not_4 (not_4_out, Vy);
  and and_15 (and_15_out, and_10_out, Vy);
  or or_8 (or_8_out, and_14_out, and_15_out, comparator_9_eq, comparator_14_eq);
  Vxy vxy_2 (.reset(reset), .change(or_5_out), .Vx(right));
  Vxy vxy_3 (.reset(reset), .change(or_8_out), .Vx(Vy));
  not not_5 (left, right);
  and and_16 (up, isVyActive, not_6_out);
  and and_17 (down, isVyActive, Vy);
  not not_6 (not_6_out, Vy);
  and and_18 (Collision, right, comparator_23_eq);
  Comparator #(.width(5), .mode("unsigned")) comparator_23 (
    .a(ballX), .b(5'b00100), .eq(comparator_23_eq));  // open: gt, lt

  assign Vx = right;

  // Notes on the sheet:
  //   Ball
endmodule

module Vxy (
  input  reset,
  input  change,
  output Vx
);

  wire adder_1_out;

  Adder #(.width(1)) adder_1 (.a(Vx), .b(1'b1), .out(adder_1_out));  // open: cin, cout
  Register #(.width(1)) register_1 (.D(adder_1_out), .en(1'b1), .Q(Vx), .clk(change), .clr(reset));
endmodule

module RandBatPos (
  input  [4:0] BatPos,
  output [4:0] RandBatPos
);

  wire clock_1_out, comparator_1_eq, comparator_2_lt;
  wire [1:0] adder_1_out, multiplexer_1_out, register_1_q;
  wire [4:0] bit_extender_1_out, subtractor_1_out;

  Adder #(.width(2)) adder_1 (.a(register_1_q), .b(2'b01), .out(adder_1_out));  // open: cin, cout
  Register #(.width(2)) register_1 (.D(adder_1_out), .Q(register_1_q), .clk(clock_1_out));  // open: en, clr
  Clock #(.highDuration(2)) clock_1 (.out(clock_1_out));
  Comparator #(.width(2), .mode("unsigned")) comparator_1 (
    .a(register_1_q), .b(2'b11), .eq(comparator_1_eq));  // open: gt, lt
  // Probe on multiplexer_1_out
  Multiplexer #(.width(2)) multiplexer_1 (
    .in0(register_1_q), .in1(2'b01), .out(multiplexer_1_out), .sel(comparator_1_eq));  // open: en
  assign bit_extender_1_out = {{3{1'b0}}, multiplexer_1_out};  // Bit_Extender bit_extender_1
  Subtractor #(.width(5)) subtractor_1 (.a(BatPos), .b(bit_extender_1_out), .out(subtractor_1_out));  // open: bin, bout
  Comparator #(.width(5), .mode("unsigned")) comparator_2 (
    .a(BatPos), .b(subtractor_1_out), .lt(comparator_2_lt));  // open: gt, eq
  // Probe on RandBatPos
  Multiplexer #(.width(5)) multiplexer_2 (
    .in0(subtractor_1_out), .in1({5{1'b0}}), .out(RandBatPos), .sel(comparator_2_lt));  // open: en
endmodule

module rightbatYWanted (
  input  [4:0] ballX,
  input  [4:0] rightbatY,
  input  [4:0] rightbatYWanted,
  input  rightBatStop,
  input  reset,
  output up,
  output down
);

  wire adder_1_out, comparator_1_eq, comparator_2_lt, comparator_3_gt, comparator_3_lt, multiplexer_1_out,
       register_1_q;
  wire [4:0] multiplexer_2_out;

  and and_1 (up, comparator_3_lt, comparator_2_lt);
  and and_2 (down, comparator_2_lt, comparator_3_gt);
  Comparator #(.width(1)) comparator_1 (.a(register_1_q), .b(1'b1), .eq(comparator_1_eq));  // open: gt, lt
  Comparator #(.width(5), .mode("unsigned")) comparator_2 (
    .a(ballX), .b(5'b10000), .lt(comparator_2_lt));  // open: gt, eq
  Adder #(.width(1)) adder_1 (.a(register_1_q), .b(multiplexer_1_out), .out(adder_1_out));  // open: cin, cout
  Multiplexer multiplexer_1 (.in0(1'b1), .in1(1'b0), .out(multiplexer_1_out), .sel(comparator_1_eq));  // open: en
  Comparator #(.width(5), .mode("unsigned")) comparator_3 (
    .a(rightbatY), .b(multiplexer_2_out), .gt(comparator_3_gt), .lt(comparator_3_lt));  // open: eq
  Multiplexer #(.width(5)) multiplexer_2 (
    .in0(5'b01110), .in1(rightbatYWanted), .out(multiplexer_2_out), .sel(register_1_q));  // open: en
  Register #(.width(1)) register_1 (.D(adder_1_out), .en(1'b1), .Q(register_1_q), .clk(rightBatStop), .clr(reset));
endmodule
